# Fritzing sketch Layout (saved by Fritzing 0.9.3b)

parts:
  Part1 = Adafruit Feather M0 RFM9x LoRa [part_number="Adafruit #3178 or #3179"]
  Part2 = sx1509 breakout
  Part3 = sx1509 breakout

nets:
  GND: Part1.GND, Part2.GND, Part3.GND
  3.3V: Part1.+3V3, Part2.3.3V, Part3.3.3V
  N1: Part1.SCL, Part2.SCL, Part3.SCL
  N2: Part1.SDA, Part2.SDA, Part3.SDA

custom parts:
  Adafruit Feather M0 RFM9x LoRa: This is the Adafruit Feather M0 RFM95 LoRa Radio - our take on an microcontroller with a "Long Range (LoRa)" packet radio transceiver with built in USB and battery charging. Its an Adafruit Feather M0 with a 433Mhz or 900MHz radio module cooked in! Great for making wireless networks that are more flexible than Bluetooth LE and without the high power requirements of WiFi. We have other boards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
